// Logisim project smips.circ as structural Verilog
module Board (
);

  wire CLK, HALT, MEM_WE, RESET, TTY_WE;
  wire [3:0] MEM_BE;
  wire [6:0] TTY_DATA;
  wire [31:0] MEM_ADDR, MEM_RDATA, MEM_WDATA;

  Clock Reloj (.out(CLK));
  Button u_Reset (.out(RESET));
  CPU cpu_1 (
    .CLK(CLK), .RESET(RESET), .MEM_RDATA(MEM_RDATA), .MEM_ADDR(MEM_ADDR), .MEM_WDATA(MEM_WDATA),
    .MEM_BE(MEM_BE), .MEM_WE(MEM_WE), .TTY_DATA(TTY_DATA), .TTY_WE(TTY_WE), .HALT(HALT));
  TTY #(.cols(48), .rows(12)) tty_1 (.data(TTY_DATA), .clk(CLK), .we(TTY_WE), .clr(RESET));
  Memory memory_1 (.CLK(CLK), .ADDR(MEM_ADDR), .WDATA(MEM_WDATA), .BE(MEM_BE), .WE(MEM_WE), .RDATA(MEM_RDATA));
  LED u_Halt (.in(HALT));

  // Notes on the sheet:
  //   S-MIPS | Board
  //   No modificar: la CPU se implementa dentro del subcircuito CPU.
endmodule

module CPU (
  input  CLK,
  input  [31:0] MEM_ADDR,
  input  RESET,
  input  [31:0] MEM_WDATA,
  input  [31:0] MEM_RDATA,
  input  [3:0] MEM_BE,
  input  MEM_WE,
  input  [6:0] TTY_DATA,
  input  TTY_WE,
  input  HALT
);


  // Notes on the sheet:
  //   CPU S-MIPS: implementar aqui
  //   No cambiar nombres, anchos ni sentido de los pines: la placa depende de ellos.
endmodule

module Memory (
  input  CLK,
  input  [31:0] RDATA,
  input  [31:0] ADDR,
  input  [31:0] WDATA,
  input  [3:0] BE,
  input  WE
);

  RAM #(.addrWidth(12), .dataWidth(32)) ram_1 (.addr(ADDR[13:2]));  // open: data, sel, clk, ld, clr

  // Other names for the same wires on the sheet: A[11:0] = ADDR[13:2]

  // Notes on the sheet:
  //   Memoria unificada: 4096 palabras de 32 bits (16 KiB), little-endian
  //   Lectura combinacional; escritura en el flanco de subida de CLK con WE=1, solo en los bytes con BE=1.
  //   Se usan los bits 13..2 de ADDR; los demas se ignoran (el espacio se repite cada 16 KiB).
endmodule

module ALU (
  input  [2:0] in_1,
  input  [31:0] in_2,
  input  [31:0] in_3,
  input  in_4,
  output Zero_Flag,
  output [31:0] out_6,
  output Equal_Flag
);

  wire comparator_1_lt;
  wire [31:0] ADD, AND, COMP_SIGNED, LOGICAL_LEFT, LOGICAL_RIGHT, MINUS, OR;

  // Probe on in_2
  // Probe on in_2
  Adder #(.width(32)) adder_1 (.a(in_2), .b(in_3), .out(ADD));  // open: cin, cout
  Subtractor #(.width(32)) subtractor_1 (.a(in_2), .b(in_3), .out(MINUS));  // open: bin, bout
  Comparator #(.width(32)) comparator_1 (.a(in_2), .b(in_3), .eq(Equal_Flag), .lt(comparator_1_lt));  // open: gt
  Shifter #(.shift("lr"), .width(32)) shifter_1 (.in(in_2), .\dist (in_3[4:0]), .out(LOGICAL_LEFT));
  Shifter #(.shift("lr"), .width(32)) shifter_2 (.in(in_2), .\dist (in_3[4:0]), .out(LOGICAL_RIGHT));
  // Probe on in_3
  // Probe on in_3
  assign AND = in_2 & in_3;  // AND_Gate and_1, 32 bits wide
  assign OR = in_2 | in_3;  // OR_Gate or_1, 32 bits wide
  assign COMP_SIGNED = {{31{comparator_1_lt}}, comparator_1_lt};  // Bit_Extender bit_extender_1
  // Probe on in_1
  // Probe on out_6
  // Probe on out_6
  Multiplexer #(.enable("true"), .select(3), .width(32)) multiplexer_1 (
    .in0(ADD), .in1(MINUS), .in2(AND), .in3(OR), .in4(COMP_SIGNED), .in5(LOGICAL_LEFT), .in6(LOGICAL_RIGHT),
    .in7(in_3), .out(out_6), .sel(in_1));  // open: en
  Comparator #(.width(32)) comparator_2 (.a({32{1'b0}}), .b(out_6), .eq(Zero_Flag));  // open: gt, lt

  // Other names for the same wires on the sheet: A[31:0] = in_2; B[31:0] = in_3; CLK = in_4; EQUAL = Equal_Flag;
  //   MAIN[31:0] = out_6; OP[2:0] = in_1; ZERO = Zero_Flag

  // Notes on the sheet:
  //   0000
  //   0001
  //   0010
  //   0011
  //   0100
  //   0101
  //   0110
  //   INPUTS
  //   OUTPUTS
endmodule

// VHDL entity register_file, as the project stores it:
library ieee;
use ieee.std_logic_1164.all;
use ieee.numeric_std.all;
entity register_file is
    port (
        clk   : in  std_logic;
        rst   : in  std_logic;
        we    : in  std_logic;                      -- Write Enable
        wa    : in  std_logic_vector(4 downto 0);   -- Write Address (rd / rt)
        wd    : in  std_logic_vector(31 downto 0);  -- Write Data
        ra1   : in  std_logic_vector(4 downto 0);   -- Read Address 1 (rs)
        ra2   : in  std_logic_vector(4 downto 0);   -- Read Address 2 (rt)
        rd1   : out std_logic_vector(31 downto 0);  -- Read Data 1
        rd2   : out std_logic_vector(31 downto 0)   -- Read Data 2
    );
end entity register_file;

architecture rtl of register_file is
    -- Definición del banco de 32 registros de 32 bits
    type reg_array is array (0 to 31) of std_logic_vector(31 downto 0);
    signal regs : reg_array;
begin

    -- Puerto de lectura 1 (Combinacional / Asíncrono)
    -- Si la dirección es 0 ($zero), retorna siempre 0.
    process(ra1, regs)
    begin
        if to_integer(unsigned(ra1)) = 0 then
            rd1 <= (others => '0');
        else
            rd1 <= regs(to_integer(unsigned(ra1)));
        end if;
    end process;

    -- Puerto de lectura 2 (Combinacional / Asíncrono)
    -- Si la dirección es 0 ($zero), retorna siempre 0.
    process(ra2, regs)
    begin
        if to_integer(unsigned(ra2)) = 0 then
            rd2 <= (others => '0');
        else
            rd2 <= regs(to_integer(unsigned(ra2)));
        end if;
    end process;

    -- Puerto de escritura (Síncrono al flanco de subida del reloj)
    process(clk)
    begin
        if rising_edge(clk) then
            if rst = '1' then
                -- Inicialización por reset según especificación [R6]
                for i in 0 to 31 loop
                    regs(i) <= (others => '0');
                end loop;
                regs(28) <= x"00001800"; 
                regs(29) <= x"00003FFC";
            else
                -- Escritura condicional (el registro $zero / $0 nunca se modifica)
                if we = '1' and to_integer(unsigned(wa)) /= 0 then
                    regs(to_integer(unsigned(wa))) <= wd;
                end if;
                -- Garantizar por seguridad que $zero permanezca en 0
                regs(0) <= (others => '0');
            end if;
        end if;
    end process;
end architecture rtl;
